// Digital circuit HW2.2.dig as structural Verilog
module HW2_2 (
  input  W,
  input  X,
  input  Y,
  input  W_2,
  input  X_2,
  input  Y_2,
  output G,
  output G_2
);

  wire nand_1_out, nand_2_out, nand_3_out, nand_4_out, nand_5_out, nand_6_out, nand_7_out, nand_8_out,
       nand_9_out, nand_10_out, nand_11_out, nand_12_out, nand_13_out, nand_14_out, nand_15_out, nand_16_out,
       nand_17_out, nand_18_out, nand_19_out, nand_20_out, nand_21_out, nand_22_out, nand_24_out, nand_25_out;

  nand nand_1 (nand_1_out, X, X);
  nand nand_2 (nand_2_out, Y, Y);
  nand nand_3 (nand_3_out, Y_2, Y_2);
  nand nand_4 (nand_4_out, nand_1_out, nand_1_out);
  nand nand_5 (nand_5_out, Y, Y);
  nand nand_6 (nand_6_out, Y_2, Y_2);
  nand nand_7 (nand_7_out, nand_4_out, nand_5_out);
  nand nand_8 (nand_8_out, X_2, nand_6_out);
  nand nand_9 (nand_9_out, W, nand_7_out);
  nand nand_10 (nand_10_out, W, Y);
  nand nand_11 (nand_11_out, W_2, nand_8_out);
  nand nand_12 (nand_12_out, W_2, Y_2);
  nand nand_13 (nand_13_out, nand_10_out, nand_10_out);
  nand nand_14 (nand_14_out, X, X);
  nand nand_15 (nand_15_out, nand_13_out, nand_13_out);
  nand nand_16 (nand_16_out, X_2, X_2);
  nand nand_17 (nand_17_out, nand_14_out, nand_15_out);
  nand nand_18 (nand_18_out, nand_16_out, nand_12_out);
  nand nand_19 (nand_19_out, nand_17_out, nand_2_out);
  nand nand_20 (nand_20_out, nand_18_out, nand_3_out);
  nand nand_21 (nand_21_out, nand_9_out, nand_9_out);
  nand nand_22 (nand_22_out, nand_19_out, nand_19_out);
  nand nand_23 (G_2, nand_11_out, nand_20_out);
  nand nand_24 (nand_24_out, nand_21_out, nand_21_out);
  nand nand_25 (nand_25_out, nand_22_out, nand_22_out);
  nand nand_26 (G, nand_24_out, nand_25_out);
endmodule
