// Digital circuit HW2.3.dig as structural Verilog
module HW2_3 (
  input  in_1,
  input  in_2,
  input  in_3,
  input  in_4,
  output out_5
);

  wire and_1_out, not_1_out, not_2_out, not_3_out, xor_1_out;

  not not_1 (not_1_out, in_1);
  not not_2 (not_2_out, in_2);
  xor xor_1 (xor_1_out, in_1, in_2);
  and and_1 (and_1_out, not_1_out, not_2_out, in_3, xor_1_out);
  not not_3 (not_3_out, in_4);
  or or_1 (out_5, in_1, not_3_out, and_1_out);
endmodule
