// Digital circuit HW2.4.dig as structural Verilog
module HW2_4 (
  input  A,
  input  B,
  input  C,
  input  D,
  input  A_2,
  input  B_2,
  input  C_2,
  input  D_2,
  input  A_3,
  input  B_3,
  input  C_3,
  input  D_3,
  output F,
  output G,
  output F_2,
  output G_2
);

  wire and_1_out, and_2_out, and_3_out, and_4_out, and_5_out, and_6_out, and_7_out, and_8_out, and_9_out,
       and_10_out, and_11_out, and_12_out, not_1_out, not_2_out, not_3_out, not_4_out, not_5_out, not_6_out,
       not_7_out, not_8_out, not_9_out, not_10_out, not_11_out, not_12_out;

  not not_1 (not_1_out, A);
  not not_2 (not_2_out, B);
  not not_3 (not_3_out, C);
  not not_4 (not_4_out, D);
  not not_5 (not_5_out, A_2);
  not not_6 (not_6_out, B_2);
  not not_7 (not_7_out, C_2);
  not not_8 (not_8_out, D_2);
  not not_9 (not_9_out, A_3);
  not not_10 (not_10_out, B_3);
  not not_11 (not_11_out, C_3);
  not not_12 (not_12_out, D_3);
  and and_1 (and_1_out, not_1_out, not_2_out);
  and and_2 (and_2_out, A, B, not_3_out);
  and and_3 (and_3_out, not_1_out, C);
  and and_4 (and_4_out, not_2_out, not_4_out);
  and and_5 (and_5_out, not_5_out, not_6_out);
  and and_6 (and_6_out, A_2, D_2, not_7_out);
  and and_7 (and_7_out, not_6_out, not_8_out);
  and and_8 (and_8_out, not_9_out, not_10_out);
  and and_9 (and_9_out, A_3, B_3, not_11_out);
  and and_10 (and_10_out, not_9_out, C_3);
  and and_11 (and_11_out, A_3, not_11_out, D_3);
  and and_12 (and_12_out, not_10_out, not_12_out);
  or or_1 (F, and_1_out, and_2_out, and_3_out, and_4_out);
  or or_2 (G, and_5_out, and_6_out, and_7_out);
  or or_3 (G_2, and_8_out, and_11_out, and_12_out);
  or or_4 (F_2, and_8_out, and_9_out, and_10_out, and_12_out);
endmodule
