// Digital circuit HW2.dig as structural Verilog
module HW2 (
  input  W1,
  input  W2,
  input  W3,
  input  W4,
  input  M1,
  input  M2,
  input  S,
  input  T,
  input  Bin,
  input  Pin,
  output Bout,
  output Pout
);

  wire and_1_out, and_2_out, or_1_out, or_2_out, or_3_out;

  or or_1 (or_1_out, W1, W2, W3, W4);
  or or_2 (or_2_out, M1, M2);
  and and_1 (and_1_out, or_2_out, T);
  or or_3 (or_3_out, or_1_out, and_1_out);
  and and_2 (and_2_out, or_3_out, S);
  and and_3 (Bout, and_2_out, Bin);
  and and_4 (Pout, and_2_out, Pin);
endmodule
